// Logisim project akkumulator.circ as structural Verilog: 3 circuits, main circuit Akkumulator
module Universalregister (
  input  d3,
  input  d2,
  input  d1,
  input  d0,
  input  dl,
  input  dr,
  input  [1:0] s,
  output q3,
  output q2,
  output q1,
  output q0
);

  wire clock_1_out, multiplexer_1_out, multiplexer_2_out, multiplexer_3_out, multiplexer_4_out;

  Clock clock_1 (.out(clock_1_out));
  Multiplexer #(.select(2), .enable("false")) multiplexer_1 (
    .in0(d3), .in1(dl), .in2(q2), .in3(q3), .out(multiplexer_1_out), .sel(s));
  Multiplexer #(.select(2), .enable("false")) multiplexer_2 (
    .in0(d2), .in1(q3), .in2(q1), .in3(q2), .out(multiplexer_2_out), .sel(s));
  D_Flip_Flop d_ff_1 (.clk(clock_1_out), .D(multiplexer_1_out), .Q(q3));  // open: Qn, preset, en, reset
  Multiplexer #(.select(2), .enable("false")) multiplexer_3 (
    .in0(d1), .in1(q2), .in2(q0), .in3(q1), .out(multiplexer_3_out), .sel(s));
  D_Flip_Flop d_ff_2 (.clk(clock_1_out), .D(multiplexer_2_out), .Q(q2));  // open: Qn, preset, en, reset
  Multiplexer #(.select(2), .enable("false")) multiplexer_4 (
    .in0(d0), .in1(q1), .in2(dr), .in3(q0), .out(multiplexer_4_out), .sel(s));
  D_Flip_Flop d_ff_3 (.clk(clock_1_out), .D(multiplexer_3_out), .Q(q1));  // open: Qn, preset, en, reset
  D_Flip_Flop d_ff_4 (.clk(clock_1_out), .D(multiplexer_4_out), .Q(q0));  // open: Qn, preset, en, reset
endmodule

module Akkumulator (
  input  d3,
  input  d2,
  input  d1,
  input  d0,
  input  s3,
  input  s2,
  input  s1,
  input  s0,
  input  dl,
  input  dr,
  output c,
  output q3,
  output q2,
  output q1,
  output q0
);

  wire [3:0] multiplexer_1_out, rechenwerk_1_z0;

  Multiplexer #(.width(4), .enable("false")) multiplexer_1 (
    .in0(rechenwerk_1_z0), .in1({d3, d2, d1, d0}), .out(multiplexer_1_out), .sel(s3));
  Universalregister universalregister_1 (
    .dl(dl), .s({s1, s0}), .dr(dr), .d3(multiplexer_1_out[3]), .d2(multiplexer_1_out[2]),
    .d1(multiplexer_1_out[1]), .d0(multiplexer_1_out[0]), .q3(q3), .q2(q2), .q1(q1), .q0(q0));
  Rechenwerk rechenwerk_1 (
    .x3(q3), .y3(d3), .x2(q2), .y2(d2), .x1(q1), .y1(d1), .x0(q0), .y0(d0), .z3(rechenwerk_1_z0[3]),
    .z2(rechenwerk_1_z0[2]), .z1(rechenwerk_1_z0[1]), .z0(rechenwerk_1_z0[0]), .c_2(c), .c(s2));
endmodule

module Rechenwerk (
  input  x3,
  input  y3,
  input  x2,
  input  y2,
  input  x1,
  input  y1,
  input  x0,
  input  y0,
  input  c,
  output c_2,
  output z3,
  output z2,
  output z1,
  output z0
);

  wire adder_2_cout, adder_3_cout, adder_4_cout, xor_1_out, xor_2_out, xor_3_out, xor_4_out;

  xor xor_1 (xor_1_out, c, y3);
  xor xor_2 (xor_2_out, c, y2);
  xor xor_3 (xor_3_out, c, y1);
  xor xor_4 (xor_4_out, c, y0);
  Adder #(.width(1)) adder_1 (.a(x3), .b(xor_1_out), .out(z3), .cin(adder_2_cout), .cout(c_2));
  Adder #(.width(1)) adder_2 (.a(x2), .b(xor_2_out), .out(z2), .cin(adder_3_cout), .cout(adder_2_cout));
  Adder #(.width(1)) adder_3 (.a(x1), .b(xor_3_out), .out(z1), .cin(adder_4_cout), .cout(adder_3_cout));
  Adder #(.width(1)) adder_4 (.a(x0), .b(xor_4_out), .out(z0), .cin(c), .cout(adder_4_cout));
endmodule
