// Logisim project ampel.circ as structural Verilog: 1 circuit, main circuit main
module main (
);

  wire and_1_out, and_2_out, and_3_out, clock_1_out, or_1_out, q0_q, q0_qn, q1_q, q1_qn;

  Clock clock_1 (.out(clock_1_out));
  D_Flip_Flop q1 (.clk(clock_1_out), .D(or_1_out), .Q(q1_q), .Qn(q1_qn));  // open: preset, en, reset
  D_Flip_Flop q0 (.clk(clock_1_out), .D(q0_qn), .Q(q0_q), .Qn(q0_qn));  // open: preset, en, reset
  and and_1 (and_1_out, q1_q, q0_qn);
  and and_2 (and_2_out, q1_q, q0_qn);
  and and_3 (and_3_out, q1_qn, q0_q);
  or or_1 (or_1_out, and_2_out, and_3_out);
  LED led_1 (.in(q1_qn));
  LED led_2 (.in(q0_q));
  LED led_3 (.in(and_1_out));

  // Notes on the sheet:
  //   Steuerwerk
  //   Datenpfad
endmodule
