// Logisim project ampel2.circ as structural Verilog: 1 circuit, main circuit main
module main (
);

  wire and_1_out, and_2_out, and_3_out, and_4_out, and_5_out, and_6_out, and_7_out, and_8_out, clock_1_out,
       or_1_out, or_2_out, or_3_out, q0_q, q0_qn, q1_q, q1_qn, q2_q, q2_qn;

  Clock clock_1 (.out(clock_1_out));
  D_Flip_Flop q2 (.clk(clock_1_out), .D(or_2_out), .Q(q2_q), .Qn(q2_qn));  // open: preset, en, reset
  D_Flip_Flop q1 (.clk(clock_1_out), .D(or_1_out), .Q(q1_q), .Qn(q1_qn));  // open: preset, en, reset
  D_Flip_Flop q0 (.clk(clock_1_out), .D(q0_qn), .Q(q0_q), .Qn(q0_qn));  // open: preset, en, reset
  and and_1 (and_1_out, q1_q, q0_qn);
  and and_2 (and_2_out, q1_qn, q0_q);
  or or_1 (or_1_out, and_1_out, and_2_out);
  and and_3 (and_3_out, q2_q, q0_qn);
  and and_4 (and_4_out, q2_qn, q1_q, q0_q);
  or or_2 (or_2_out, and_4_out, and_3_out, and_5_out);
  and and_5 (and_5_out, q2_q, q1_qn);
  and and_6 (and_6_out, q1_q, q0_q);
  or or_3 (or_3_out, and_8_out, and_7_out);
  and and_7 (and_7_out, q2_q, q0_qn);
  and and_8 (and_8_out, q2_q, q1_qn);
  LED led_1 (.in(q2_qn));
  LED led_2 (.in(and_6_out));
  LED led_3 (.in(or_3_out));

  // Notes on the sheet:
  //   Steuerwerk
  //   Datenpfad
endmodule
