// Logisim project barrelShifter.circ as structural Verilog: 1 circuit, main circuit main
module main (
  input  b3,
  input  b2,
  input  b1,
  input  b0,
  input  Mode,
  input  [2:0] Dir_x1_x0,
  output b3_prime,
  output b2_prime,
  output b1_prime,
  output b0_prime
);

  wire multiplexer_1_out;

  Multiplexer #(.enable("false")) multiplexer_1 (.in0(1'b0), .in1(b3), .out(multiplexer_1_out), .sel(Mode));
  Multiplexer #(.select(3), .enable("false")) multiplexer_2 (
    .in0(b3), .in1(b2), .in2(b1), .in3(b0), .in4(b3), .in5(multiplexer_1_out), .in6(multiplexer_1_out),
    .in7(multiplexer_1_out), .out(b3_prime), .sel(Dir_x1_x0));
  Multiplexer #(.select(3), .enable("false")) multiplexer_3 (
    .in0(b2), .in1(b1), .in2(b0), .in3(1'b0), .in4(b2), .in5(b3), .in6(multiplexer_1_out),
    .in7(multiplexer_1_out), .out(b2_prime), .sel(Dir_x1_x0));
  Multiplexer #(.select(3), .enable("false")) multiplexer_4 (
    .in0(b1), .in1(b0), .in2(1'b0), .in3(1'b0), .in4(b1), .in5(b2), .in6(b3), .in7(multiplexer_1_out),
    .out(b1_prime), .sel(Dir_x1_x0));
  Multiplexer #(.select(3), .enable("false")) multiplexer_5 (
    .in0(b0), .in1(1'b0), .in2(1'b0), .in3(1'b0), .in4(b0), .in5(b1), .in6(b2), .in7(b3), .out(b0_prime),
    .sel(Dir_x1_x0));
endmodule
