// Logisim project claa.circ as structural Verilog: 4 circuits, main circuit main
// CLAA
module carry_look_ahead_addierer (
  input  a3,
  input  b3,
  input  a2,
  input  b2,
  input  a1,
  input  b1,
  input  a0,
  input  b0,
  input  c0,
  output s3,
  output s2,
  output s1,
  output s0,
  output c4,
  output G,
  output P
);

  wire carry_look_ahead_generator_1_c1, carry_look_ahead_generator_1_c2, carry_look_ahead_generator_1_c3,
       volladdierer_1_g, volladdierer_1_p, volladdierer_2_g, volladdierer_2_p, volladdierer_3_g,
       volladdierer_3_p, volladdierer_4_g, volladdierer_4_p;

  volladdierer volladdierer_1 (
    .a_n(a3), .b_n(b3), .c_in(carry_look_ahead_generator_1_c3), .g(volladdierer_1_g), .p(volladdierer_1_p),
    .sum(s3));
  volladdierer volladdierer_2 (
    .a_n(a2), .b_n(b2), .c_in(carry_look_ahead_generator_1_c2), .g(volladdierer_2_g), .p(volladdierer_2_p),
    .sum(s2));
  carry_look_ahead_generator carry_look_ahead_generator_1 (
    .c1(carry_look_ahead_generator_1_c1), .c2(carry_look_ahead_generator_1_c2),
    .c3(carry_look_ahead_generator_1_c3), .c4(c4), .g3(volladdierer_1_g), .p3(volladdierer_1_p),
    .g2(volladdierer_2_g), .p2(volladdierer_2_p), .g1(volladdierer_3_g), .p1(volladdierer_3_p),
    .g0(volladdierer_4_g), .p0(volladdierer_4_p), .c0(c0), .P(P), .G(G));
  volladdierer volladdierer_3 (
    .a_n(a1), .b_n(b1), .c_in(carry_look_ahead_generator_1_c1), .g(volladdierer_3_g), .p(volladdierer_3_p),
    .sum(s1));
  volladdierer volladdierer_4 (.a_n(a0), .b_n(b0), .c_in(c0), .g(volladdierer_4_g), .p(volladdierer_4_p), .sum(s0));
endmodule

// VA
module volladdierer (
  input  a_n,
  input  b_n,
  input  c_in,
  output g,
  output p,
  output sum
);

  and and_1 (g, a_n, b_n);
  xor xor_1 (p, a_n, b_n);
  xor xor_2 (sum, p, c_in);
endmodule

// CLAG
module carry_look_ahead_generator (
  input  g3,
  input  p3,
  input  g2,
  input  p2,
  input  g1,
  input  p1,
  input  g0,
  input  p0,
  input  c0,
  output c1,
  output c2,
  output c3,
  output c4,
  output G,
  output P
);

  wire and_1_out, and_2_out, and_3_out, and_4_out, and_5_out, and_6_out, and_7_out, and_8_out, and_9_out,
       and_10_out;

  and and_1 (and_1_out, c0, p0);
  and and_2 (and_2_out, c0, p0, p1);
  and and_3 (and_3_out, g0, p1);
  and and_4 (and_4_out, c0, p0, p1, p2);
  and and_5 (and_5_out, g0, p1, p2);
  and and_6 (and_6_out, g1, p2);
  and and_7 (and_7_out, c0, p0, p1, p2, p3);
  and and_8 (and_8_out, g0, p1, p2, p3);
  and and_9 (and_9_out, g1, p2, p3);
  and and_10 (and_10_out, g2, p3);
  and and_11 (P, p0, p1, p2, p3);
  or or_1 (c1, and_1_out, g0);
  or or_2 (c2, and_2_out, and_3_out, g1);
  or or_3 (c3, and_4_out, and_5_out, and_6_out, g2);
  or or_4 (c4, and_7_out, and_8_out, and_9_out, and_10_out, g3);
  or or_5 (G, and_8_out, and_9_out, and_10_out, g3);
endmodule

module main (
  input  a15,
  input  a14,
  input  a13,
  input  a12,
  input  a11,
  input  a10,
  input  a9,
  input  a8,
  input  a7,
  input  a6,
  input  a5,
  input  a4,
  input  a3,
  input  a2,
  input  a1,
  input  a0,
  input  b15,
  input  b14,
  input  b13,
  input  b12,
  input  b11,
  input  b10,
  input  b9,
  input  b8,
  input  b7,
  input  b6,
  input  b5,
  input  b4,
  input  b3,
  input  b2,
  input  b1,
  input  b0,
  input  c0,
  output sF,
  output sE,
  output sD,
  output sC,
  output sB,
  output sA,
  output s9,
  output s8,
  output s7,
  output s6,
  output s5,
  output s4,
  output s3,
  output s2,
  output s1,
  output s0,
  output c4,
  output G,
  output P
);

  wire carry_look_ahead_addierer_1_g, carry_look_ahead_addierer_1_p, carry_look_ahead_addierer_2_g,
       carry_look_ahead_addierer_2_p, carry_look_ahead_addierer_3_g, carry_look_ahead_addierer_3_p,
       carry_look_ahead_addierer_4_g, carry_look_ahead_addierer_4_p, carry_look_ahead_generator_1_c1,
       carry_look_ahead_generator_1_c2, carry_look_ahead_generator_1_c3;

  carry_look_ahead_addierer carry_look_ahead_addierer_1 (
    .a3(a15), .b3(b15), .a2(a14), .b2(b14), .a1(a13), .b1(b13), .a0(a12), .b0(b12),
    .c0(carry_look_ahead_generator_1_c3), .s3(sF), .G(carry_look_ahead_addierer_1_g),
    .P(carry_look_ahead_addierer_1_p), .s2(sE), .s1(sD), .s0(sC));  // open: c4
  carry_look_ahead_addierer carry_look_ahead_addierer_2 (
    .a3(a11), .b3(b11), .a2(a10), .b2(b10), .a1(a9), .b1(b9), .a0(a8), .b0(b8),
    .c0(carry_look_ahead_generator_1_c2), .s3(sB), .G(carry_look_ahead_addierer_2_g),
    .P(carry_look_ahead_addierer_2_p), .s2(sA), .s1(s9), .s0(s8));  // open: c4
  carry_look_ahead_addierer carry_look_ahead_addierer_3 (
    .a3(a7), .b3(b7), .a2(a6), .b2(b6), .a1(a5), .b1(b5), .a0(a4), .b0(b4),
    .c0(carry_look_ahead_generator_1_c1), .s3(s7), .G(carry_look_ahead_addierer_3_g),
    .P(carry_look_ahead_addierer_3_p), .s2(s6), .s1(s5), .s0(s4));  // open: c4
  carry_look_ahead_generator carry_look_ahead_generator_1 (
    .c1(carry_look_ahead_generator_1_c1), .c2(carry_look_ahead_generator_1_c2),
    .c3(carry_look_ahead_generator_1_c3), .c4(c4), .g3(carry_look_ahead_addierer_1_g),
    .p3(carry_look_ahead_addierer_1_p), .g2(carry_look_ahead_addierer_2_g),
    .p2(carry_look_ahead_addierer_2_p), .g1(carry_look_ahead_addierer_3_g),
    .p1(carry_look_ahead_addierer_3_p), .g0(carry_look_ahead_addierer_4_g),
    .p0(carry_look_ahead_addierer_4_p), .c0(c0), .P(P), .G(G));
  carry_look_ahead_addierer carry_look_ahead_addierer_4 (
    .a3(a3), .b3(b3), .a2(a2), .b2(b2), .a1(a1), .b1(b1), .a0(a0), .b0(b0), .c0(c0), .s3(s3),
    .G(carry_look_ahead_addierer_4_g), .P(carry_look_ahead_addierer_4_p), .s2(s2), .s1(s1), .s0(s0));  // open: c4
endmodule
