// Logisim project claaSiebensegment.circ as structural Verilog: 6 circuits, main circuit main
// CLAA
module carry_look_ahead_addierer (
  input  a3,
  input  b3,
  input  a2,
  input  b2,
  input  a1,
  input  b1,
  input  a0,
  input  b0,
  input  c0,
  output s3,
  output s2,
  output s1,
  output s0,
  output c4,
  output G,
  output P
);

  wire carry_look_ahead_generator_1_c1, carry_look_ahead_generator_1_c2, carry_look_ahead_generator_1_c3,
       volladdierer_1_g, volladdierer_1_p, volladdierer_2_g, volladdierer_2_p, volladdierer_3_g,
       volladdierer_3_p, volladdierer_4_g, volladdierer_4_p;

  volladdierer volladdierer_1 (
    .a_n(a3), .b_n(b3), .c_in(carry_look_ahead_generator_1_c3), .g(volladdierer_1_g), .p(volladdierer_1_p),
    .sum(s3));
  volladdierer volladdierer_2 (
    .a_n(a2), .b_n(b2), .c_in(carry_look_ahead_generator_1_c2), .g(volladdierer_2_g), .p(volladdierer_2_p),
    .sum(s2));
  carry_look_ahead_generator carry_look_ahead_generator_1 (
    .c1(carry_look_ahead_generator_1_c1), .c2(carry_look_ahead_generator_1_c2),
    .c3(carry_look_ahead_generator_1_c3), .c4(c4), .g3(volladdierer_1_g), .p3(volladdierer_1_p),
    .g2(volladdierer_2_g), .p2(volladdierer_2_p), .g1(volladdierer_3_g), .p1(volladdierer_3_p),
    .g0(volladdierer_4_g), .p0(volladdierer_4_p), .c0(c0), .P(P), .G(G));
  volladdierer volladdierer_3 (
    .a_n(a1), .b_n(b1), .c_in(carry_look_ahead_generator_1_c1), .g(volladdierer_3_g), .p(volladdierer_3_p),
    .sum(s1));
  volladdierer volladdierer_4 (.a_n(a0), .b_n(b0), .c_in(c0), .g(volladdierer_4_g), .p(volladdierer_4_p), .sum(s0));
endmodule

// VA
module volladdierer (
  input  a_n,
  input  b_n,
  input  c_in,
  output g,
  output p,
  output sum
);

  and and_1 (g, a_n, b_n);
  xor xor_1 (p, a_n, b_n);
  xor xor_2 (sum, p, c_in);
endmodule

// CLAG
module carry_look_ahead_generator (
  input  g3,
  input  p3,
  input  g2,
  input  p2,
  input  g1,
  input  p1,
  input  g0,
  input  p0,
  input  c0,
  output c1,
  output c2,
  output c3,
  output c4,
  output G,
  output P
);

  wire and_1_out, and_2_out, and_3_out, and_4_out, and_5_out, and_6_out, and_7_out, and_8_out, and_9_out,
       and_10_out;

  and and_1 (and_1_out, c0, p0);
  and and_2 (and_2_out, c0, p0, p1);
  and and_3 (and_3_out, g0, p1);
  and and_4 (and_4_out, c0, p0, p1, p2);
  and and_5 (and_5_out, g0, p1, p2);
  and and_6 (and_6_out, g1, p2);
  and and_7 (and_7_out, c0, p0, p1, p2, p3);
  and and_8 (and_8_out, g0, p1, p2, p3);
  and and_9 (and_9_out, g1, p2, p3);
  and and_10 (and_10_out, g2, p3);
  and and_11 (P, p0, p1, p2, p3);
  or or_1 (c1, and_1_out, g0);
  or or_2 (c2, and_2_out, and_3_out, g1);
  or or_3 (c3, and_4_out, and_5_out, and_6_out, g2);
  or or_4 (c4, and_7_out, and_8_out, and_9_out, and_10_out, g3);
  or or_5 (G, and_8_out, and_9_out, and_10_out, g3);
endmodule

module main (
  input  a15,
  input  a14,
  input  a13,
  input  a12,
  input  a11,
  input  a10,
  input  a9,
  input  a8,
  input  a7,
  input  a6,
  input  a5,
  input  a4,
  input  a3,
  input  a2,
  input  a1,
  input  a0,
  input  b15,
  input  b14,
  input  b13,
  input  b12,
  input  b11,
  input  b10,
  input  b9,
  input  b8,
  input  b7,
  input  b6,
  input  b5,
  input  b4,
  input  b3,
  input  b2,
  input  b1,
  input  b0,
  input  c0,
  output c4,
  output G,
  output P
);

  wire carry_look_ahead_addierer_1_g, carry_look_ahead_addierer_1_p, carry_look_ahead_addierer_2_g,
       carry_look_ahead_addierer_2_p, carry_look_ahead_addierer_3_g, carry_look_ahead_addierer_3_p,
       carry_look_ahead_addierer_4_g, carry_look_ahead_addierer_4_p, carry_look_ahead_generator_1_c1,
       carry_look_ahead_generator_1_c2, carry_look_ahead_generator_1_c3;
  wire [3:0] carry_look_ahead_addierer_1_s0, carry_look_ahead_addierer_2_s0, carry_look_ahead_addierer_3_s0,
       carry_look_ahead_addierer_4_s0, dezimaldekoder_1_b0, dezimaldekoder_1_b1, dezimaldekoder_1_b2,
       dezimaldekoder_1_b3, dezimaldekoder_1_b4, dezimaldekoder_2_b0, dezimaldekoder_2_b1,
       dezimaldekoder_2_b2, dezimaldekoder_2_b3, dezimaldekoder_2_b4, dezimaldekoder_3_b0,
       dezimaldekoder_3_b1, dezimaldekoder_3_b2, dezimaldekoder_3_b3, dezimaldekoder_3_b4,
       siebendekoder_1_d1, siebendekoder_1_d5, siebendekoder_2_d1, siebendekoder_2_d5, siebendekoder_3_d1,
       siebendekoder_3_d5, siebendekoder_4_d1, siebendekoder_4_d5, siebendekoder_5_d1, siebendekoder_5_d5,
       siebendekoder_6_d1, siebendekoder_6_d5, siebendekoder_7_d1, siebendekoder_7_d5, siebendekoder_8_d1,
       siebendekoder_8_d5, siebendekoder_9_d1, siebendekoder_9_d5, siebendekoder_10_d1, siebendekoder_10_d5,
       siebendekoder_11_d1, siebendekoder_11_d5, siebendekoder_12_d1, siebendekoder_12_d5,
       siebendekoder_13_d1, siebendekoder_13_d5, siebendekoder_14_d1, siebendekoder_14_d5,
       siebendekoder_15_d1, siebendekoder_15_d5;

  carry_look_ahead_addierer carry_look_ahead_addierer_1 (
    .a3(a15), .b3(b15), .a2(a14), .b2(b14), .a1(a13), .b1(b13), .a0(a12), .b0(b12),
    .c0(carry_look_ahead_generator_1_c3), .s3(carry_look_ahead_addierer_1_s0[3]),
    .G(carry_look_ahead_addierer_1_g), .P(carry_look_ahead_addierer_1_p),
    .s2(carry_look_ahead_addierer_1_s0[2]), .s1(carry_look_ahead_addierer_1_s0[1]),
    .s0(carry_look_ahead_addierer_1_s0[0]));  // open: c4
  carry_look_ahead_addierer carry_look_ahead_addierer_2 (
    .a3(a11), .b3(b11), .a2(a10), .b2(b10), .a1(a9), .b1(b9), .a0(a8), .b0(b8),
    .c0(carry_look_ahead_generator_1_c2), .s3(carry_look_ahead_addierer_2_s0[3]),
    .G(carry_look_ahead_addierer_2_g), .P(carry_look_ahead_addierer_2_p),
    .s2(carry_look_ahead_addierer_2_s0[2]), .s1(carry_look_ahead_addierer_2_s0[1]),
    .s0(carry_look_ahead_addierer_2_s0[0]));  // open: c4
  carry_look_ahead_addierer carry_look_ahead_addierer_3 (
    .a3(a7), .b3(b7), .a2(a6), .b2(b6), .a1(a5), .b1(b5), .a0(a4), .b0(b4),
    .c0(carry_look_ahead_generator_1_c1), .s3(carry_look_ahead_addierer_3_s0[3]),
    .G(carry_look_ahead_addierer_3_g), .P(carry_look_ahead_addierer_3_p),
    .s2(carry_look_ahead_addierer_3_s0[2]), .s1(carry_look_ahead_addierer_3_s0[1]),
    .s0(carry_look_ahead_addierer_3_s0[0]));  // open: c4
  carry_look_ahead_generator carry_look_ahead_generator_1 (
    .c1(carry_look_ahead_generator_1_c1), .c2(carry_look_ahead_generator_1_c2),
    .c3(carry_look_ahead_generator_1_c3), .c4(c4), .g3(carry_look_ahead_addierer_1_g),
    .p3(carry_look_ahead_addierer_1_p), .g2(carry_look_ahead_addierer_2_g),
    .p2(carry_look_ahead_addierer_2_p), .g1(carry_look_ahead_addierer_3_g),
    .p1(carry_look_ahead_addierer_3_p), .g0(carry_look_ahead_addierer_4_g),
    .p0(carry_look_ahead_addierer_4_p), .c0(c0), .P(P), .G(G));
  carry_look_ahead_addierer carry_look_ahead_addierer_4 (
    .a3(a3), .b3(b3), .a2(a2), .b2(b2), .a1(a1), .b1(b1), .a0(a0), .b0(b0), .c0(c0),
    .s3(carry_look_ahead_addierer_4_s0[3]), .G(carry_look_ahead_addierer_4_g),
    .P(carry_look_ahead_addierer_4_p), .s2(carry_look_ahead_addierer_4_s0[2]),
    .s1(carry_look_ahead_addierer_4_s0[1]), .s0(carry_look_ahead_addierer_4_s0[0]));  // open: c4
  _7_Segment_Display u_7_segment_display_1 (
    .g(siebendekoder_1_d1[0]), .f(siebendekoder_1_d1[1]), .a(siebendekoder_1_d1[2]),
    .b(siebendekoder_1_d1[3]), .e(siebendekoder_1_d5[0]), .d(siebendekoder_1_d5[1]),
    .c(siebendekoder_1_d5[2]), .dp(siebendekoder_1_d5[3]));
  dezimaldekoder dezimaldekoder_1 (
    .in_1({a15, a14, a13, a12, a11, a10, a9, a8, a7, a6, a5, a4, a3, a2, a1, a0}), .B0(dezimaldekoder_1_b0),
    .B1(dezimaldekoder_1_b1), .B2(dezimaldekoder_1_b2), .B3(dezimaldekoder_1_b3), .B4(dezimaldekoder_1_b4));
  _7_Segment_Display u_7_segment_display_2 (
    .g(siebendekoder_2_d1[0]), .f(siebendekoder_2_d1[1]), .a(siebendekoder_2_d1[2]),
    .b(siebendekoder_2_d1[3]), .e(siebendekoder_2_d5[0]), .d(siebendekoder_2_d5[1]),
    .c(siebendekoder_2_d5[2]), .dp(siebendekoder_2_d5[3]));
  dezimaldekoder dezimaldekoder_2 (
    .in_1({b15, b14, b13, b12, b11, b10, b9, b8, b7, b6, b5, b4, b3, b2, b1, b0}), .B0(dezimaldekoder_2_b0),
    .B1(dezimaldekoder_2_b1), .B2(dezimaldekoder_2_b2), .B3(dezimaldekoder_2_b3), .B4(dezimaldekoder_2_b4));
  _7_Segment_Display u_7_segment_display_3 (
    .g(siebendekoder_3_d1[0]), .f(siebendekoder_3_d1[1]), .a(siebendekoder_3_d1[2]),
    .b(siebendekoder_3_d1[3]), .e(siebendekoder_3_d5[0]), .d(siebendekoder_3_d5[1]),
    .c(siebendekoder_3_d5[2]), .dp(siebendekoder_3_d5[3]));
  dezimaldekoder dezimaldekoder_3 (
    .in_1({carry_look_ahead_addierer_1_s0, carry_look_ahead_addierer_2_s0, carry_look_ahead_addierer_3_s0, carry_look_ahead_addierer_4_s0}),
    .B0(dezimaldekoder_3_b0), .B1(dezimaldekoder_3_b1), .B2(dezimaldekoder_3_b2), .B3(dezimaldekoder_3_b3),
    .B4(dezimaldekoder_3_b4));
  siebendekoder siebendekoder_1 (
    .x0(dezimaldekoder_1_b4[0]), .x1(dezimaldekoder_1_b4[1]), .x2(dezimaldekoder_1_b4[2]),
    .x3(dezimaldekoder_1_b4[3]), .d2(siebendekoder_1_d1[1]), .d3(siebendekoder_1_d1[2]),
    .d4(siebendekoder_1_d1[3]), .d5(siebendekoder_1_d5[0]), .d1(siebendekoder_1_d1[0]),
    .d7(siebendekoder_1_d5[2]), .d6(siebendekoder_1_d5[1]), .d8(siebendekoder_1_d5[3]));
  siebendekoder siebendekoder_2 (
    .x0(dezimaldekoder_2_b4[0]), .x1(dezimaldekoder_2_b4[1]), .x2(dezimaldekoder_2_b4[2]),
    .x3(dezimaldekoder_2_b4[3]), .d2(siebendekoder_2_d1[1]), .d3(siebendekoder_2_d1[2]),
    .d4(siebendekoder_2_d1[3]), .d5(siebendekoder_2_d5[0]), .d1(siebendekoder_2_d1[0]),
    .d7(siebendekoder_2_d5[2]), .d6(siebendekoder_2_d5[1]), .d8(siebendekoder_2_d5[3]));
  siebendekoder siebendekoder_3 (
    .x0(dezimaldekoder_3_b4[0]), .x1(dezimaldekoder_3_b4[1]), .x2(dezimaldekoder_3_b4[2]),
    .x3(dezimaldekoder_3_b4[3]), .d2(siebendekoder_3_d1[1]), .d3(siebendekoder_3_d1[2]),
    .d4(siebendekoder_3_d1[3]), .d5(siebendekoder_3_d5[0]), .d1(siebendekoder_3_d1[0]),
    .d7(siebendekoder_3_d5[2]), .d6(siebendekoder_3_d5[1]), .d8(siebendekoder_3_d5[3]));
  _7_Segment_Display u_7_segment_display_4 (
    .g(siebendekoder_4_d1[0]), .f(siebendekoder_4_d1[1]), .a(siebendekoder_4_d1[2]),
    .b(siebendekoder_4_d1[3]), .e(siebendekoder_4_d5[0]), .d(siebendekoder_4_d5[1]),
    .c(siebendekoder_4_d5[2]), .dp(siebendekoder_4_d5[3]));
  siebendekoder siebendekoder_4 (
    .x0(dezimaldekoder_1_b3[0]), .x1(dezimaldekoder_1_b3[1]), .x2(dezimaldekoder_1_b3[2]),
    .x3(dezimaldekoder_1_b3[3]), .d2(siebendekoder_4_d1[1]), .d3(siebendekoder_4_d1[2]),
    .d4(siebendekoder_4_d1[3]), .d5(siebendekoder_4_d5[0]), .d1(siebendekoder_4_d1[0]),
    .d7(siebendekoder_4_d5[2]), .d6(siebendekoder_4_d5[1]), .d8(siebendekoder_4_d5[3]));
  _7_Segment_Display u_7_segment_display_5 (
    .g(siebendekoder_5_d1[0]), .f(siebendekoder_5_d1[1]), .a(siebendekoder_5_d1[2]),
    .b(siebendekoder_5_d1[3]), .e(siebendekoder_5_d5[0]), .d(siebendekoder_5_d5[1]),
    .c(siebendekoder_5_d5[2]), .dp(siebendekoder_5_d5[3]));
  siebendekoder siebendekoder_5 (
    .x0(dezimaldekoder_2_b3[0]), .x1(dezimaldekoder_2_b3[1]), .x2(dezimaldekoder_2_b3[2]),
    .x3(dezimaldekoder_2_b3[3]), .d2(siebendekoder_5_d1[1]), .d3(siebendekoder_5_d1[2]),
    .d4(siebendekoder_5_d1[3]), .d5(siebendekoder_5_d5[0]), .d1(siebendekoder_5_d1[0]),
    .d7(siebendekoder_5_d5[2]), .d6(siebendekoder_5_d5[1]), .d8(siebendekoder_5_d5[3]));
  _7_Segment_Display u_7_segment_display_6 (
    .g(siebendekoder_6_d1[0]), .f(siebendekoder_6_d1[1]), .a(siebendekoder_6_d1[2]),
    .b(siebendekoder_6_d1[3]), .e(siebendekoder_6_d5[0]), .d(siebendekoder_6_d5[1]),
    .c(siebendekoder_6_d5[2]), .dp(siebendekoder_6_d5[3]));
  siebendekoder siebendekoder_6 (
    .x0(dezimaldekoder_3_b3[0]), .x1(dezimaldekoder_3_b3[1]), .x2(dezimaldekoder_3_b3[2]),
    .x3(dezimaldekoder_3_b3[3]), .d2(siebendekoder_6_d1[1]), .d3(siebendekoder_6_d1[2]),
    .d4(siebendekoder_6_d1[3]), .d5(siebendekoder_6_d5[0]), .d1(siebendekoder_6_d1[0]),
    .d7(siebendekoder_6_d5[2]), .d6(siebendekoder_6_d5[1]), .d8(siebendekoder_6_d5[3]));
  _7_Segment_Display u_7_segment_display_7 (
    .g(siebendekoder_7_d1[0]), .f(siebendekoder_7_d1[1]), .a(siebendekoder_7_d1[2]),
    .b(siebendekoder_7_d1[3]), .e(siebendekoder_7_d5[0]), .d(siebendekoder_7_d5[1]),
    .c(siebendekoder_7_d5[2]), .dp(siebendekoder_7_d5[3]));
  siebendekoder siebendekoder_7 (
    .x0(dezimaldekoder_1_b2[0]), .x1(dezimaldekoder_1_b2[1]), .x2(dezimaldekoder_1_b2[2]),
    .x3(dezimaldekoder_1_b2[3]), .d2(siebendekoder_7_d1[1]), .d3(siebendekoder_7_d1[2]),
    .d4(siebendekoder_7_d1[3]), .d5(siebendekoder_7_d5[0]), .d1(siebendekoder_7_d1[0]),
    .d7(siebendekoder_7_d5[2]), .d6(siebendekoder_7_d5[1]), .d8(siebendekoder_7_d5[3]));
  _7_Segment_Display u_7_segment_display_8 (
    .g(siebendekoder_8_d1[0]), .f(siebendekoder_8_d1[1]), .a(siebendekoder_8_d1[2]),
    .b(siebendekoder_8_d1[3]), .e(siebendekoder_8_d5[0]), .d(siebendekoder_8_d5[1]),
    .c(siebendekoder_8_d5[2]), .dp(siebendekoder_8_d5[3]));
  siebendekoder siebendekoder_8 (
    .x0(dezimaldekoder_2_b2[0]), .x1(dezimaldekoder_2_b2[1]), .x2(dezimaldekoder_2_b2[2]),
    .x3(dezimaldekoder_2_b2[3]), .d2(siebendekoder_8_d1[1]), .d3(siebendekoder_8_d1[2]),
    .d4(siebendekoder_8_d1[3]), .d5(siebendekoder_8_d5[0]), .d1(siebendekoder_8_d1[0]),
    .d7(siebendekoder_8_d5[2]), .d6(siebendekoder_8_d5[1]), .d8(siebendekoder_8_d5[3]));
  _7_Segment_Display u_7_segment_display_9 (
    .g(siebendekoder_9_d1[0]), .f(siebendekoder_9_d1[1]), .a(siebendekoder_9_d1[2]),
    .b(siebendekoder_9_d1[3]), .e(siebendekoder_9_d5[0]), .d(siebendekoder_9_d5[1]),
    .c(siebendekoder_9_d5[2]), .dp(siebendekoder_9_d5[3]));
  siebendekoder siebendekoder_9 (
    .x0(dezimaldekoder_3_b2[0]), .x1(dezimaldekoder_3_b2[1]), .x2(dezimaldekoder_3_b2[2]),
    .x3(dezimaldekoder_3_b2[3]), .d2(siebendekoder_9_d1[1]), .d3(siebendekoder_9_d1[2]),
    .d4(siebendekoder_9_d1[3]), .d5(siebendekoder_9_d5[0]), .d1(siebendekoder_9_d1[0]),
    .d7(siebendekoder_9_d5[2]), .d6(siebendekoder_9_d5[1]), .d8(siebendekoder_9_d5[3]));
  _7_Segment_Display u_7_segment_display_10 (
    .g(siebendekoder_10_d1[0]), .f(siebendekoder_10_d1[1]), .a(siebendekoder_10_d1[2]),
    .b(siebendekoder_10_d1[3]), .e(siebendekoder_10_d5[0]), .d(siebendekoder_10_d5[1]),
    .c(siebendekoder_10_d5[2]), .dp(siebendekoder_10_d5[3]));
  siebendekoder siebendekoder_10 (
    .x0(dezimaldekoder_1_b1[0]), .x1(dezimaldekoder_1_b1[1]), .x2(dezimaldekoder_1_b1[2]),
    .x3(dezimaldekoder_1_b1[3]), .d2(siebendekoder_10_d1[1]), .d3(siebendekoder_10_d1[2]),
    .d4(siebendekoder_10_d1[3]), .d5(siebendekoder_10_d5[0]), .d1(siebendekoder_10_d1[0]),
    .d7(siebendekoder_10_d5[2]), .d6(siebendekoder_10_d5[1]), .d8(siebendekoder_10_d5[3]));
  _7_Segment_Display u_7_segment_display_11 (
    .g(siebendekoder_11_d1[0]), .f(siebendekoder_11_d1[1]), .a(siebendekoder_11_d1[2]),
    .b(siebendekoder_11_d1[3]), .e(siebendekoder_11_d5[0]), .d(siebendekoder_11_d5[1]),
    .c(siebendekoder_11_d5[2]), .dp(siebendekoder_11_d5[3]));
  siebendekoder siebendekoder_11 (
    .x0(dezimaldekoder_2_b1[0]), .x1(dezimaldekoder_2_b1[1]), .x2(dezimaldekoder_2_b1[2]),
    .x3(dezimaldekoder_2_b1[3]), .d2(siebendekoder_11_d1[1]), .d3(siebendekoder_11_d1[2]),
    .d4(siebendekoder_11_d1[3]), .d5(siebendekoder_11_d5[0]), .d1(siebendekoder_11_d1[0]),
    .d7(siebendekoder_11_d5[2]), .d6(siebendekoder_11_d5[1]), .d8(siebendekoder_11_d5[3]));
  _7_Segment_Display u_7_segment_display_12 (
    .g(siebendekoder_12_d1[0]), .f(siebendekoder_12_d1[1]), .a(siebendekoder_12_d1[2]),
    .b(siebendekoder_12_d1[3]), .e(siebendekoder_12_d5[0]), .d(siebendekoder_12_d5[1]),
    .c(siebendekoder_12_d5[2]), .dp(siebendekoder_12_d5[3]));
  siebendekoder siebendekoder_12 (
    .x0(dezimaldekoder_3_b1[0]), .x1(dezimaldekoder_3_b1[1]), .x2(dezimaldekoder_3_b1[2]),
    .x3(dezimaldekoder_3_b1[3]), .d2(siebendekoder_12_d1[1]), .d3(siebendekoder_12_d1[2]),
    .d4(siebendekoder_12_d1[3]), .d5(siebendekoder_12_d5[0]), .d1(siebendekoder_12_d1[0]),
    .d7(siebendekoder_12_d5[2]), .d6(siebendekoder_12_d5[1]), .d8(siebendekoder_12_d5[3]));
  _7_Segment_Display u_7_segment_display_13 (
    .g(siebendekoder_13_d1[0]), .f(siebendekoder_13_d1[1]), .a(siebendekoder_13_d1[2]),
    .b(siebendekoder_13_d1[3]), .e(siebendekoder_13_d5[0]), .d(siebendekoder_13_d5[1]),
    .c(siebendekoder_13_d5[2]), .dp(siebendekoder_13_d5[3]));
  siebendekoder siebendekoder_13 (
    .x0(dezimaldekoder_1_b0[0]), .x1(dezimaldekoder_1_b0[1]), .x2(dezimaldekoder_1_b0[2]),
    .x3(dezimaldekoder_1_b0[3]), .d2(siebendekoder_13_d1[1]), .d3(siebendekoder_13_d1[2]),
    .d4(siebendekoder_13_d1[3]), .d5(siebendekoder_13_d5[0]), .d1(siebendekoder_13_d1[0]),
    .d7(siebendekoder_13_d5[2]), .d6(siebendekoder_13_d5[1]), .d8(siebendekoder_13_d5[3]));
  _7_Segment_Display u_7_segment_display_14 (
    .g(siebendekoder_14_d1[0]), .f(siebendekoder_14_d1[1]), .a(siebendekoder_14_d1[2]),
    .b(siebendekoder_14_d1[3]), .e(siebendekoder_14_d5[0]), .d(siebendekoder_14_d5[1]),
    .c(siebendekoder_14_d5[2]), .dp(siebendekoder_14_d5[3]));
  siebendekoder siebendekoder_14 (
    .x0(dezimaldekoder_2_b0[0]), .x1(dezimaldekoder_2_b0[1]), .x2(dezimaldekoder_2_b0[2]),
    .x3(dezimaldekoder_2_b0[3]), .d2(siebendekoder_14_d1[1]), .d3(siebendekoder_14_d1[2]),
    .d4(siebendekoder_14_d1[3]), .d5(siebendekoder_14_d5[0]), .d1(siebendekoder_14_d1[0]),
    .d7(siebendekoder_14_d5[2]), .d6(siebendekoder_14_d5[1]), .d8(siebendekoder_14_d5[3]));
  _7_Segment_Display u_7_segment_display_15 (
    .g(siebendekoder_15_d1[0]), .f(siebendekoder_15_d1[1]), .a(siebendekoder_15_d1[2]),
    .b(siebendekoder_15_d1[3]), .e(siebendekoder_15_d5[0]), .d(siebendekoder_15_d5[1]),
    .c(siebendekoder_15_d5[2]), .dp(siebendekoder_15_d5[3]));
  siebendekoder siebendekoder_15 (
    .x0(dezimaldekoder_3_b0[0]), .x1(dezimaldekoder_3_b0[1]), .x2(dezimaldekoder_3_b0[2]),
    .x3(dezimaldekoder_3_b0[3]), .d2(siebendekoder_15_d1[1]), .d3(siebendekoder_15_d1[2]),
    .d4(siebendekoder_15_d1[3]), .d5(siebendekoder_15_d5[0]), .d1(siebendekoder_15_d1[0]),
    .d7(siebendekoder_15_d5[2]), .d6(siebendekoder_15_d5[1]), .d8(siebendekoder_15_d5[3]));

  // Notes on the sheet:
  //   Summe
  //   Summand 1
  //   Summand 2
endmodule

// DezDek
module dezimaldekoder (
  input  [15:0] in_1,
  output [3:0] B0,
  output [3:0] B1,
  output [3:0] B2,
  output [3:0] B3,
  output [3:0] B4
);

  wire [15:0] divider_1_out, divider_2_out, divider_3_out, divider_4_out;
  wire [15:4] divider_1_rem, divider_2_rem, divider_3_rem, divider_4_rem, divider_5_rem;

  Divider #(.width(16)) divider_1 (.a(in_1), .b(16'ha), .out(divider_1_out), .rem({divider_1_rem, B0}));  // open: upper
  Divider #(.width(16)) divider_2 (
    .a(divider_1_out), .b(16'ha), .out(divider_2_out), .rem({divider_2_rem, B1}));  // open: upper
  Divider #(.width(16)) divider_3 (
    .a(divider_2_out), .b(16'ha), .out(divider_3_out), .rem({divider_3_rem, B2}));  // open: upper
  Divider #(.width(16)) divider_4 (
    .a(divider_3_out), .b(16'ha), .out(divider_4_out), .rem({divider_4_rem, B3}));  // open: upper
  Divider #(.width(16)) divider_5 (.a(divider_4_out), .b(16'ha), .rem({divider_5_rem, B4}));  // open: out, upper
endmodule

// SieDek
module siebendekoder (
  input  x0,
  input  x1,
  input  x2,
  input  x3,
  output d2,
  output d3,
  output d4,
  output d5,
  output d1,
  output d7,
  output d6,
  output d8
);

  wire and_4_out, and_5_out, not_1_out, not_2_out, not_3_out, not_4_out, or_1_out, or_2_out, or_3_out,
       or_4_out, or_5_out, or_6_out, or_7_out, or_9_out, or_10_out, or_12_out, or_13_out, or_14_out;

  not not_1 (not_1_out, x0);
  not not_2 (not_2_out, x1);
  not not_3 (not_3_out, x2);
  not not_4 (not_4_out, x3);
  or or_1 (or_1_out, x3, x2, not_1_out);
  or or_2 (or_2_out, not_2_out, not_1_out);
  or or_3 (or_3_out, x3, x2, not_2_out);
  and and_1 (d2, or_1_out, or_3_out, or_2_out);
  or or_4 (or_4_out, x3, x2, x1, not_1_out);
  and and_2 (d3, or_4_out, or_5_out);
  or or_5 (or_5_out, not_3_out, x1, x0);
  or or_6 (or_6_out, not_3_out, x1, not_1_out);
  and and_3 (d4, or_6_out, or_7_out);
  or or_7 (or_7_out, not_3_out, not_2_out, x0);
  and and_4 (and_4_out, not_3_out, not_1_out);
  or or_8 (d5, and_4_out, and_5_out);
  and and_5 (and_5_out, x1, not_1_out);
  or or_9 (or_9_out, x3, x2, x1);
  and and_6 (d1, or_9_out, or_10_out);
  or or_10 (or_10_out, not_3_out, not_2_out, not_1_out);
  or or_11 (d7, x2, not_2_out, x0);
  or or_12 (or_12_out, x3, x2, x1, not_1_out);
  or or_13 (or_13_out, not_3_out, not_2_out, not_1_out);
  or or_14 (or_14_out, not_3_out, x1, x0);
  and and_7 (d6, or_12_out, or_14_out, or_13_out);
  and and_8 (d8, x0, not_1_out);
endmodule
