// Logisim project dLatch.circ as structural Verilog: 1 circuit, main circuit main
module main (
  input  D,
  input  T,
  output Q_prime,
  output Q
);

  wire and_1_out, not_1_out;

  and and_1 (and_1_out, D, T);
  not not_1 (not_1_out, and_1_out);
  nor nor_1 (Q_prime, and_1_out, Q);
  nor nor_2 (Q, Q_prime, not_1_out);
endmodule
