// Logisim project halbaddierer.circ as structural Verilog: 1 circuit, main circuit main
module main (
  input  b1,
  input  b2,
  output Sum,
  output Carry
);

  xor xor_1 (Sum, b1, b2);
  and and_1 (Carry, b1, b2);
endmodule
