// Logisim project happyXMAS.circ as structural Verilog: 9 circuits, main circuit main
module main (
  output b3,
  output b2,
  output b1,
  output b0
);

  wire C_out, d_ff_1_q, d_ff_2_q, d_ff_3_q, d_ff_4_q, next0_1_q0_prime, next1_1_q1_prime, next2_1_q2_prime,
       next3_1_q3_prime;

  Clock C (.out(C_out));
  next3 next3_1 (.q3(d_ff_1_q), .q2(d_ff_2_q), .q1(d_ff_3_q), .q0(d_ff_4_q), .q3_prime(next3_1_q3_prime));
  next2 next2_1 (.q3(d_ff_1_q), .q2(d_ff_2_q), .q1(d_ff_3_q), .q0(d_ff_4_q), .q2_prime(next2_1_q2_prime));
  D_Flip_Flop d_ff_1 (.clk(C_out), .D(next3_1_q3_prime), .Q(d_ff_1_q));  // open: Qn, preset, en, reset
  next1 next1_1 (.q3(d_ff_1_q), .q2(d_ff_2_q), .q1(d_ff_3_q), .q0(d_ff_4_q), .q1_prime(next1_1_q1_prime));
  D_Flip_Flop d_ff_2 (.clk(C_out), .D(next2_1_q2_prime), .Q(d_ff_2_q));  // open: Qn, preset, en, reset
  D_Flip_Flop d_ff_3 (.clk(C_out), .D(next1_1_q1_prime), .Q(d_ff_3_q));  // open: Qn, preset, en, reset
  next0 next0_1 (.q3(d_ff_1_q), .q2(d_ff_2_q), .q1(d_ff_3_q), .q0(d_ff_4_q), .q0_prime(next0_1_q0_prime));
  D_Flip_Flop d_ff_4 (.clk(C_out), .D(next0_1_q0_prime), .Q(d_ff_4_q));  // open: Qn, preset, en, reset
  b3 b3_1 (.q3(d_ff_1_q), .q2(d_ff_2_q), .q1(d_ff_3_q), .q0(d_ff_4_q), .b3(b3));
  b2 b2_1 (.q3(d_ff_1_q), .q2(d_ff_2_q), .q1(d_ff_3_q), .q0(d_ff_4_q), .b2(b2));
  b1 b1_1 (.q3(d_ff_1_q), .q2(d_ff_2_q), .q1(d_ff_3_q), .q0(d_ff_4_q), .b1(b1));
  b0 b0_1 (.q3(d_ff_1_q), .q2(d_ff_2_q), .q1(d_ff_3_q), .q0(d_ff_4_q), .b0(b0));

  // Notes on the sheet:
  //   q3
  //   q2
  //   q1
  //   q0
endmodule

// n0
module next0 (
  input  q3,
  input  q2,
  input  q1,
  input  q0,
  output q0_prime
);

  not not_1 (q0_prime, q0);
endmodule

// n1
module next1 (
  input  q3,
  input  q2,
  input  q1,
  input  q0,
  output q1_prime
);

  wire and_1_out, and_2_out;

  and and_1 (and_1_out, q1, ~q0);  // AND_Gate
  and and_2 (and_2_out, ~q3, ~q1, q0);  // AND_Gate
  or or_1 (q1_prime, and_1_out, and_2_out);
endmodule

// n2
module next2 (
  input  q3,
  input  q2,
  input  q1,
  input  q0,
  output q2_prime
);

  wire and_1_out, and_2_out, and_3_out;

  and and_1 (and_1_out, q2, ~q1);  // AND_Gate
  and and_2 (and_2_out, ~q2, q1, q0);  // AND_Gate
  and and_3 (and_3_out, q2, ~q0);  // AND_Gate
  or or_1 (q2_prime, and_1_out, and_2_out, and_3_out);
endmodule

// n3
module next3 (
  input  q3,
  input  q2,
  input  q1,
  input  q0,
  output q3_prime
);

  wire and_1_out, and_2_out;

  and and_1 (and_1_out, q3, ~q0);  // AND_Gate
  and and_2 (and_2_out, q2, q1, q0);
  or or_1 (q3_prime, and_1_out, and_2_out);
endmodule

module b3 (
  input  q3,
  input  q2,
  input  q1,
  input  q0,
  output b3
);

  wire and_1_out, and_2_out;

  and and_1 (and_1_out, ~q3, ~q1, ~q0);  // AND_Gate
  and and_2 (and_2_out, q2, q1);
  or or_1 (b3, and_1_out, and_2_out);
endmodule

module b2 (
  input  q3,
  input  q2,
  input  q1,
  input  q0,
  output b2
);

  and and_1 (b2, q2, q1, q0);
endmodule

module b1 (
  input  q3,
  input  q2,
  input  q1,
  input  q0,
  output b1
);

  and and_1 (b1, q3, q0);
endmodule

module b0 (
  input  q3,
  input  q2,
  input  q1,
  input  q0,
  output b0
);

  wire and_1_out, and_2_out, and_3_out;

  and and_1 (and_1_out, q2, q1, q0);
  and and_2 (and_2_out, q2, ~q1, ~q0);  // AND_Gate
  and and_3 (and_3_out, ~q2, ~q1, q0);  // AND_Gate
  or or_1 (b0, q3, and_1_out, and_2_out, and_3_out);
endmodule
