// Logisim project mikroprozessor (In Konflikt stehende Kopie von lars-ThinkPad-X230 2013-01-31).circ as structural Verilog
module main (
);

  wire [3:0] ram_1_data;
  wire [7:0] undriven;
  wire [7:4] ram_1_data_2;

  Register #(.width(4)) register_1 (.D(ram_1_data_2));  // open: en, Q, clk, clr
  Register #(.width(4)) register_2 (.D(ram_1_data));  // open: en, Q, clk, clr
  RAM ram_1 (.addr(undriven), .data({ram_1_data_2, ram_1_data}), .sel(1'b1), .ld(1'b1), .clr(1'b0));  // open: clk
endmodule
