// Logisim project mikroprozessor.circ as structural Verilog: 2 circuits, main circuit main
module main (
);

  wire [3:0] ram_1_data, undriven;
  wire [7:0] undriven_2;
  wire [7:4] ram_1_data_2;

  Register #(.width(4)) register_1 (.D(ram_1_data_2));  // open: en, Q, clk, clr
  Register #(.width(4)) register_2 (.D(ram_1_data));  // open: en, Q, clk, clr
  Akkumulator akkumulator_1 (
    .d3(undriven[3]), .d2(undriven[2]), .d1(undriven[1]), .d0(undriven[0]));  // open: s3, s2, clk, c, q3, q2, q1, q0
  RAM ram_1 (.addr(undriven_2), .data({ram_1_data_2, ram_1_data}), .sel(1'b1), .ld(1'b1), .clr(1'b0));  // open: clk
endmodule

module Akkumulator (
  input  d3,
  input  d2,
  input  d1,
  input  d0,
  input  s3,
  input  s2,
  input  clk,
  output c,
  output q3,
  output q2,
  output q1,
  output q0
);

  wire [4:0] multiplexer_1_out, rechenwerk_1_z3;

  Multiplexer #(.width(5), .enable("false")) multiplexer_1 (
    .in0(rechenwerk_1_z3), .in1({1'b0, d3, d2, d1, d0}), .out(multiplexer_1_out), .sel(s3));
  Register #(.width(5)) register_1 (.D(multiplexer_1_out), .en(1'b1), .Q({q0, q1, q2, q3, c}), .clk(clk), .clr(1'b0));
  Rechenwerk rechenwerk_1 (
    .x3(q3), .y3(d3), .x2(q2), .y2(d2), .x1(q1), .y1(d1), .x0(q0), .y0(d0), .z3(rechenwerk_1_z3[0]),
    .z2(rechenwerk_1_z3[1]), .z1(rechenwerk_1_z3[2]), .z0(rechenwerk_1_z3[3]), .c_2(rechenwerk_1_z3[4]),
    .c(s2));
endmodule
