// Logisim project mikroprozessorBuch.circ as structural Verilog: 6 circuits, main circuit main
module main (
);

  wire clk_out, instruktionsdekoder_1_add, instruktionsdekoder_1_brc, instruktionsdekoder_1_brn,
       instruktionsdekoder_1_brz, instruktionsdekoder_1_dir, instruktionsdekoder_1_jmp,
       instruktionsdekoder_1_lda, instruktionsdekoder_1_nop, instruktionsdekoder_1_sta,
       instruktionsdekoder_1_sub, m1, steuerwerk_1_clk_prime, steuerwerk_1_clk_prime_2,
       steuerwerk_1_clk_prime_3, steuerwerk_1_e, steuerwerk_1_ld, steuerwerk_1_m2, steuerwerk_1_s0,
       steuerwerk_1_s1, steuerwerk_1_sub_2, steuerwerk_1_we;
  wire [2:0] akkumulator_1_c, akkumulator_1_q0, ZCN_q;
  wire [3:0] DR_q, \instruktionszähler_1_q0 , IR_q, multiplexer_1_out, multiplexer_2_out, ram_1_data,
       ram_2_data;

  Clock clk (.out(clk_out));
  Register #(.width(4)) IR (.D(ram_2_data), .Q(IR_q), .clk(clk_out));  // open: en, clr
  Instruktionsdekoder instruktionsdekoder_1 (
    .q3(IR_q[3]), .q2(IR_q[2]), .q1(IR_q[1]), .q0(IR_q[0]), .brn(instruktionsdekoder_1_brn),
    .brc(instruktionsdekoder_1_brc), .brz(instruktionsdekoder_1_brz), .jmp(instruktionsdekoder_1_jmp),
    .sub(instruktionsdekoder_1_sub), .add(instruktionsdekoder_1_add), .sta(instruktionsdekoder_1_sta),
    .lda(instruktionsdekoder_1_lda), .nop(instruktionsdekoder_1_nop), .dir(instruktionsdekoder_1_dir));
  Register #(.width(4)) DR (.D(ram_1_data), .Q(DR_q), .clk(clk_out));  // open: en, clr
  Steuerwerk steuerwerk_1 (
    .e(steuerwerk_1_e), .ld(steuerwerk_1_ld), .sub_2(steuerwerk_1_sub_2), .clk_prime(steuerwerk_1_clk_prime),
    .clk_prime_2(steuerwerk_1_clk_prime_2), .s1(steuerwerk_1_s1), .s0(steuerwerk_1_s0),
    .clk_prime_3(steuerwerk_1_clk_prime_3), .we(steuerwerk_1_we), .m1(m1), .m2(steuerwerk_1_m2),
    .clk(clk_out), .brn(instruktionsdekoder_1_brn), .brc(instruktionsdekoder_1_brc),
    .brz(instruktionsdekoder_1_brz), .jmp(instruktionsdekoder_1_jmp), .sub(instruktionsdekoder_1_sub),
    .add(instruktionsdekoder_1_add), .sta(instruktionsdekoder_1_sta), .lda(instruktionsdekoder_1_lda),
    .nop(instruktionsdekoder_1_nop), .dir(instruktionsdekoder_1_dir), .c(ZCN_q[1]), .n(ZCN_q[0]), .z(ZCN_q[2]));
  Multiplexer #(.width(4), .enable("false")) multiplexer_1 (
    .in0(ram_1_data), .in1(DR_q), .out(multiplexer_1_out), .sel(m1));
  nor nor_1 (akkumulator_1_c[2], akkumulator_1_q0[0], akkumulator_1_q0[1], akkumulator_1_q0[2], akkumulator_1_c[0]);
  Register #(.width(3)) ZCN (.D(akkumulator_1_c), .Q(ZCN_q));  // open: en, clk, clr
  \Instruktionszähler  \instruktionszähler_1  (
    .d3(DR_q[3]), .d2(DR_q[2]), .d1(DR_q[1]), .d0(DR_q[0]), .s1(steuerwerk_1_s1), .s0(steuerwerk_1_s0),
    .clk(steuerwerk_1_clk_prime_3), .q3(\instruktionszähler_1_q0 [3]), .q2(\instruktionszähler_1_q0 [2]),
    .q1(\instruktionszähler_1_q0 [1]), .q0(\instruktionszähler_1_q0 [0]));
  Akkumulator akkumulator_1 (
    .d3(multiplexer_1_out[3]), .d2(multiplexer_1_out[2]), .d1(multiplexer_1_out[1]),
    .d0(multiplexer_1_out[0]), .ld(steuerwerk_1_ld), .sub(steuerwerk_1_sub_2), .en(steuerwerk_1_e),
    .clk(steuerwerk_1_clk_prime), .c(akkumulator_1_c[1]), .q3(akkumulator_1_c[0]), .q2(akkumulator_1_q0[2]),
    .q1(akkumulator_1_q0[1]), .q0(akkumulator_1_q0[0]));
  Multiplexer #(.width(4), .enable("false")) multiplexer_2 (
    .in0(DR_q), .in1(\instruktionszähler_1_q0 ), .out(multiplexer_2_out), .sel(steuerwerk_1_m2));
  RAM #(.addrWidth(4), .dataWidth(4), .bus("separate")) ram_1 (
    .addr(multiplexer_2_out), .din({akkumulator_1_c[0], akkumulator_1_q0}), .data(ram_1_data),
    .str(steuerwerk_1_we), .clk(steuerwerk_1_clk_prime_2));  // open: sel, ld, clr
  RAM #(.addrWidth(4), .dataWidth(4), .bus("asynch")) ram_2 (
    .addr(multiplexer_2_out), .data(ram_2_data));  // open: sel, ld, clr
endmodule

module Akkumulator (
  input  d3,
  input  d2,
  input  d1,
  input  d0,
  input  ld,
  input  sub,
  input  en,
  input  clk,
  output c,
  output q3,
  output q2,
  output q1,
  output q0
);

  wire [4:0] multiplexer_1_out, rechenwerk_1_z3;

  Multiplexer #(.width(5), .enable("false")) multiplexer_1 (
    .in0(rechenwerk_1_z3), .in1({1'b0, d3, d2, d1, d0}), .out(multiplexer_1_out), .sel(ld));
  Register #(.width(5)) register_1 (.D(multiplexer_1_out), .en(en), .Q({c, q3, q2, q1, q0}), .clk(clk));  // open: clr
  Rechenwerk rechenwerk_1 (
    .x3(q3), .y3(d3), .x2(q2), .y2(d2), .x1(q1), .y1(d1), .x0(q0), .y0(d0), .c_2(rechenwerk_1_z3[4]),
    .z3(rechenwerk_1_z3[0]), .z2(rechenwerk_1_z3[1]), .z1(rechenwerk_1_z3[2]), .z0(rechenwerk_1_z3[3]),
    .c(sub));
endmodule

module Rechenwerk (
  input  x3,
  input  y3,
  input  x2,
  input  y2,
  input  x1,
  input  y1,
  input  x0,
  input  y0,
  input  c,
  output c_2,
  output z3,
  output z2,
  output z1,
  output z0
);

  wire adder_2_cout, adder_3_cout, adder_4_cout, xor_1_out, xor_2_out, xor_3_out, xor_4_out;

  xor xor_1 (xor_1_out, c, y3);
  xor xor_2 (xor_2_out, c, y2);
  xor xor_3 (xor_3_out, c, y1);
  xor xor_4 (xor_4_out, c, y0);
  Adder #(.width(1)) adder_1 (.a(x3), .b(xor_1_out), .out(z3), .cin(adder_2_cout), .cout(c_2));
  Adder #(.width(1)) adder_2 (.a(x2), .b(xor_2_out), .out(z2), .cin(adder_3_cout), .cout(adder_2_cout));
  Adder #(.width(1)) adder_3 (.a(x1), .b(xor_3_out), .out(z1), .cin(adder_4_cout), .cout(adder_3_cout));
  Adder #(.width(1)) adder_4 (.a(x0), .b(xor_4_out), .out(z0), .cin(c), .cout(adder_4_cout));
endmodule

module Instruktionsdekoder (
  input  q3,
  input  q2,
  input  q1,
  input  q0,
  output brn,
  output brc,
  output brz,
  output jmp,
  output sub,
  output add,
  output sta,
  output lda,
  output nop,
  output dir
);

  wire and_5_out, and_6_out, and_7_out, and_8_out, and_10_out, and_11_out;

  and and_1 (brn, q3, ~q2, q1, q0);  // AND_Gate
  and and_2 (brc, q3, ~q2, q1, ~q0);  // AND_Gate
  and and_3 (brz, q3, ~q2, ~q1, q0);  // AND_Gate
  and and_4 (jmp, q3, ~q2, ~q1, ~q0);  // AND_Gate
  and and_5 (and_5_out, ~q3, q2, q1, q0);  // AND_Gate
  or or_1 (sub, and_5_out, and_7_out);
  and and_6 (and_6_out, ~q3, q2, ~q1, q0);  // AND_Gate
  and and_7 (and_7_out, ~q3, q2, q1, ~q0);  // AND_Gate
  and and_8 (and_8_out, ~q3, q2, ~q1, ~q0);  // AND_Gate
  or or_2 (add, and_6_out, and_8_out);
  and and_9 (sta, ~q3, ~q2, q1, q0);  // AND_Gate
  and and_10 (and_10_out, ~q3, ~q2, q1, ~q0);  // AND_Gate
  or or_3 (lda, and_10_out, and_11_out);
  and and_11 (and_11_out, ~q3, ~q2, ~q1, q0);  // AND_Gate
  and and_12 (nop, ~q3, ~q2, ~q1, ~q0);  // AND_Gate
  or or_4 (dir, and_5_out, and_6_out, and_10_out);
endmodule

module Steuerwerk (
  input  clk,
  input  brn,
  input  brc,
  input  brz,
  input  jmp,
  input  sub,
  input  add,
  input  sta,
  input  lda,
  input  nop,
  input  dir,
  input  c,
  input  n,
  input  z,
  output e,
  output ld,
  output sub_2,
  output clk_prime,
  output clk_prime_2,
  output s1,
  output s0,
  output clk_prime_3,
  output we,
  output m1,
  output m2
);

  wire and_1_out, and_2_out, and_3_out;

  or or_1 (e, lda, add, sub);
  not not_1 (clk_prime, clk);
  and and_1 (and_1_out, brz, z);
  and and_2 (and_2_out, brc, c);
  and and_3 (and_3_out, brn, n);
  not not_2 (we, sta);
  or or_2 (s1, and_1_out, and_2_out, and_3_out, jmp);

  assign clk_prime_2 = clk_prime;
  assign clk_prime_3 = clk_prime;
  assign ld = lda;
  assign m1 = dir;
  assign m2 = clk_prime;
  assign s0 = jmp;
  assign sub_2 = sub;
endmodule

module \Instruktionszähler  (
  input  d3,
  input  d2,
  input  d1,
  input  d0,
  input  s1,
  input  s0,
  input  clk,
  output q3,
  output q2,
  output q1,
  output q0
);

  wire [3:0] multiplexer_1_out, multiplexer_2_out, rechenwerk_1_z3;

  Multiplexer #(.width(4), .enable("false")) multiplexer_1 (
    .in0({d3, d2, d1, d0}), .in1(4'b0000), .out(multiplexer_1_out), .sel(s1));
  Multiplexer #(.width(4), .enable("false")) multiplexer_2 (
    .in0(rechenwerk_1_z3), .in1(multiplexer_1_out), .out(multiplexer_2_out), .sel(s0));
  Register #(.width(4)) register_1 (.D(multiplexer_2_out), .Q({q3, q2, q1, q0}), .clk(clk));  // open: en, clr
  Rechenwerk rechenwerk_1 (
    .x3(q3), .y3(multiplexer_1_out[3]), .x2(q2), .y2(multiplexer_1_out[2]), .x1(q1),
    .y1(multiplexer_1_out[1]), .x0(q0), .y0(multiplexer_1_out[0]), .z3(rechenwerk_1_z3[0]),
    .z2(rechenwerk_1_z3[1]), .z1(rechenwerk_1_z3[2]), .z0(rechenwerk_1_z3[3]), .c(1'b0));  // open: c_2
endmodule
