// Logisim project modulo10zaehler.circ as structural Verilog: 6 circuits, main circuit main
module main (
);

  wire clock_1_out, d_ff_1_q, d_ff_2_q, d_ff_3_q, d_ff_4_q, next0_1_q0_prime, next1_1_q1_prime,
       next2_1_q2_prime, next3_1_q3_prime;
  wire [6:0] nextchar_1_out_5;

  Clock clock_1 (.out(clock_1_out));
  next3 next3_1 (.q3(d_ff_1_q), .q2(d_ff_2_q), .q1(d_ff_3_q), .q0(d_ff_4_q), .q3_prime(next3_1_q3_prime));
  next2 next2_1 (.q3(d_ff_1_q), .q2(d_ff_2_q), .q1(d_ff_3_q), .q0(d_ff_4_q), .q2_prime(next2_1_q2_prime));
  D_Flip_Flop d_ff_1 (.clk(clock_1_out), .D(next3_1_q3_prime), .Q(d_ff_1_q));  // open: Qn, preset, en, reset
  next1 next1_1 (.q3(d_ff_1_q), .q2(d_ff_2_q), .q1(d_ff_3_q), .q0(d_ff_4_q), .q1_prime(next1_1_q1_prime));
  D_Flip_Flop d_ff_2 (.clk(clock_1_out), .D(next2_1_q2_prime), .Q(d_ff_2_q));  // open: Qn, preset, en, reset
  D_Flip_Flop d_ff_3 (.clk(clock_1_out), .D(next1_1_q1_prime), .Q(d_ff_3_q));  // open: Qn, preset, en, reset
  next0 next0_1 (.q3(d_ff_1_q), .q2(d_ff_2_q), .q1(d_ff_3_q), .q0(d_ff_4_q), .q0_prime(next0_1_q0_prime));
  D_Flip_Flop d_ff_4 (.clk(clock_1_out), .D(next0_1_q0_prime), .Q(d_ff_4_q));  // open: Qn, preset, en, reset
  nextChar nextchar_1 (.q3(d_ff_1_q), .q2(d_ff_2_q), .q1(d_ff_3_q), .q0(d_ff_4_q), .out_5(nextchar_1_out_5));
  TTY tty_1 (.data(nextchar_1_out_5), .clk(clock_1_out));  // open: we, clr

  // Notes on the sheet:
  //   q3
  //   q2
  //   q1
  //   q0
endmodule

// n0
module next0 (
  input  q3,
  input  q2,
  input  q1,
  input  q0,
  output q0_prime
);

  not not_1 (q0_prime, q0);
endmodule

// n1
module next1 (
  input  q3,
  input  q2,
  input  q1,
  input  q0,
  output q1_prime
);

  wire and_1_out, and_2_out;

  and and_1 (and_1_out, q1, ~q0);  // AND_Gate
  and and_2 (and_2_out, ~q3, ~q1, q0);  // AND_Gate
  or or_1 (q1_prime, and_1_out, and_2_out);
endmodule

// n2
module next2 (
  input  q3,
  input  q2,
  input  q1,
  input  q0,
  output q2_prime
);

  wire and_1_out, and_2_out, and_3_out;

  and and_1 (and_1_out, q2, ~q1);  // AND_Gate
  and and_2 (and_2_out, ~q2, q1, q0);  // AND_Gate
  and and_3 (and_3_out, q2, q1, ~q0);  // AND_Gate
  or or_1 (q2_prime, and_1_out, and_2_out, and_3_out);
endmodule

// n3
module next3 (
  input  q3,
  input  q2,
  input  q1,
  input  q0,
  output q3_prime
);

  wire and_1_out, and_2_out;

  and and_1 (and_1_out, q3, ~q0);  // AND_Gate
  and and_2 (and_2_out, q2, q1, q0);
  or or_1 (q3_prime, and_1_out, and_2_out);
endmodule

// nC
module nextChar (
  input  q3,
  input  q2,
  input  q1,
  input  q0,
  output [6:0] out_5
);

  Multiplexer #(.select(4), .width(7), .enable("false")) multiplexer_1 (
    .in0(7'b1001101), .in1(7'b1100101), .in2(7'b1110010), .in3(7'b1110010), .in4(7'b1111001),
    .in5(7'b0100000), .in6(7'b1011000), .in7(7'b1001101), .in8(7'b1000001), .in9(7'b1010011), .out(out_5),
    .sel({q3, q2, q1, q0}));  // open: in10, in11, in12, in13, in14, in15
endmodule
