// Logisim project multiplexer.circ as structural Verilog: 1 circuit, main circuit main
module main (
  input  in_1,
  input  in_2,
  input  [1:0] B,
  output out_4
);

  wire or_1_out;

  or or_1 (or_1_out, in_1, in_2);
  Multiplexer #(.select(2), .disabled(0), .enable("false")) multiplexer_1 (
    .in0(1'b1), .in1(or_1_out), .in2(or_1_out), .in3(or_1_out), .out(out_4), .sel(B));
endmodule
