// Logisim project nand.circ as structural Verilog: 1 circuit, main circuit main
module main (
  input  in_1,
  input  in_2,
  input  in_3,
  output NAND
);

  wire transistor_3_out, transistor_4_out;

  Transistor transistor_1 (.in(1'b1), .out(NAND), .gate(in_1));
  Transistor #(.\type ("n")) transistor_2 (.in(transistor_3_out), .out(NAND), .gate(in_1));
  Transistor #(.\type ("n")) transistor_3 (.in(transistor_4_out), .out(transistor_3_out), .gate(in_2));
  Transistor #(.\type ("n")) transistor_4 (.in(1'b0), .out(transistor_4_out), .gate(in_3));
  Transistor transistor_5 (.in(1'b1), .out(NAND), .gate(in_2));
  Transistor transistor_6 (.in(1'b1), .out(NAND), .gate(in_3));
endmodule
