// Logisim project rsFlipFlop.circ as structural Verilog: 2 circuits, main circuit main
module main (
  input  in_1,
  output out_2,
  output out_3,
  output out_4,
  output out_5,
  output out_6,
  output out_7,
  output out_8,
  output out_9
);

  wire not_1_out, rsflipflop_1_q_prime, rsflipflop_2_q_prime, rsflipflop_3_q_prime, rsflipflop_4_q_prime,
       rsflipflop_5_q_prime, rsflipflop_6_q_prime, rsflipflop_7_q_prime;

  not not_1 (not_1_out, in_1);
  rsFlipFlop rsflipflop_1 (.S_prime(not_1_out), .R_prime(in_1), .Q(out_2), .Q_prime(rsflipflop_1_q_prime));
  rsFlipFlop rsflipflop_2 (.S_prime(rsflipflop_1_q_prime), .R_prime(out_2), .Q(out_3), .Q_prime(rsflipflop_2_q_prime));
  rsFlipFlop rsflipflop_3 (.S_prime(rsflipflop_2_q_prime), .R_prime(out_3), .Q(out_4), .Q_prime(rsflipflop_3_q_prime));
  rsFlipFlop rsflipflop_4 (.S_prime(rsflipflop_3_q_prime), .R_prime(out_4), .Q(out_5), .Q_prime(rsflipflop_4_q_prime));
  rsFlipFlop rsflipflop_5 (.S_prime(rsflipflop_4_q_prime), .R_prime(out_5), .Q(out_6), .Q_prime(rsflipflop_5_q_prime));
  rsFlipFlop rsflipflop_6 (.S_prime(rsflipflop_5_q_prime), .R_prime(out_6), .Q(out_7), .Q_prime(rsflipflop_6_q_prime));
  rsFlipFlop rsflipflop_7 (.S_prime(rsflipflop_6_q_prime), .R_prime(out_7), .Q(out_8), .Q_prime(rsflipflop_7_q_prime));
  rsFlipFlop rsflipflop_8 (.S_prime(rsflipflop_7_q_prime), .R_prime(out_8), .Q(out_9));  // open: Q_prime
endmodule

// RS
module rsFlipFlop (
  input  S_prime,
  input  R_prime,
  output Q,
  output Q_prime
);

  wire clock_1_out, nand_1_out, nand_2_out, nand_3_out, nand_4_out;

  Clock clock_1 (.out(clock_1_out));
  nand nand_1 (nand_1_out, nand_3_out, S_prime);
  nand nand_2 (nand_2_out, R_prime, nand_4_out);
  nand nand_3 (nand_3_out, nand_1_out, clock_1_out, nand_4_out);
  nand nand_4 (nand_4_out, nand_3_out, clock_1_out, nand_2_out);
  nand nand_5 (Q, nand_3_out, Q_prime);
  nand nand_6 (Q_prime, Q, nand_4_out);
endmodule
