// Logisim project rsLatchTaktzustand.circ as structural Verilog: 1 circuit, main circuit main
module main (
  input  R,
  input  T,
  input  S,
  output Q,
  output Q_prime
);

  wire and_1_out, and_2_out;

  and and_1 (and_1_out, R, T);
  and and_2 (and_2_out, T, S);
  nor nor_1 (Q, and_1_out, Q_prime);
  nor nor_2 (Q_prime, Q, and_2_out);
endmodule
