// Logisim project schieberegister.circ as structural Verilog: 2 circuits, main circuit main
module main (
  input  d,
  output out_2,
  output out_3,
  output out_4,
  output out_5,
  output out_6,
  output out_7,
  output out_8,
  output out_9
);

  wire clock_1_out, not_1_out;

  Clock clock_1 (.out(clock_1_out));
  not not_1 (not_1_out, clock_1_out);
  D_Latch d_latch_1 (.D(d), .C(clock_1_out), .Q(out_2));  // open: Q_prime
  D_Latch d_latch_2 (.D(out_2), .C(not_1_out), .Q(out_3));  // open: Q_prime
  D_Latch d_latch_3 (.D(out_3), .C(clock_1_out), .Q(out_4));  // open: Q_prime
  D_Latch d_latch_4 (.D(out_4), .C(not_1_out), .Q(out_5));  // open: Q_prime
  D_Latch d_latch_5 (.D(out_5), .C(clock_1_out), .Q(out_6));  // open: Q_prime
  D_Latch d_latch_6 (.D(out_6), .C(not_1_out), .Q(out_7));  // open: Q_prime
  D_Latch d_latch_7 (.D(out_7), .C(clock_1_out), .Q(out_8));  // open: Q_prime
  D_Latch d_latch_8 (.D(out_8), .C(not_1_out), .Q(out_9));  // open: Q_prime
endmodule

// D
module D_Latch (
  input  D,
  input  C,
  output Q_prime,
  output Q
);

  wire and_1_out, and_2_out;

  and and_1 (and_1_out, D, C);
  and and_2 (and_2_out, ~D, C);  // AND_Gate
  nor nor_1 (Q_prime, and_1_out, Q);
  nor nor_2 (Q, Q_prime, and_2_out);
endmodule
