// Logisim project siebensegment0.circ as structural Verilog: 1 circuit, main circuit main
module main (
  input  x0,
  input  x1,
  input  x2,
  input  x3
);

  wire and_1_out, and_2_out, and_3_out, and_4_out, and_5_out, and_6_out, and_7_out, not_1_out, not_2_out,
       not_3_out, not_4_out, or_1_out, or_2_out, or_3_out, or_4_out, or_5_out, or_6_out, or_7_out, or_8_out,
       or_9_out, or_10_out, or_11_out, or_12_out, or_13_out, or_14_out;

  not not_1 (not_1_out, x0);
  not not_2 (not_2_out, x1);
  not not_3 (not_3_out, x2);
  not not_4 (not_4_out, x3);
  or or_1 (or_1_out, x3, x2, not_1_out);
  or or_2 (or_2_out, not_2_out, not_1_out);
  or or_3 (or_3_out, x3, x2, not_2_out);
  and and_1 (and_1_out, or_1_out, or_3_out, or_2_out);
  or or_4 (or_4_out, x3, x2, x1, not_1_out);
  and and_2 (and_2_out, or_4_out, or_6_out);
  or or_5 (or_5_out, not_3_out, x1, not_1_out);
  or or_6 (or_6_out, not_3_out, x1, x0);
  and and_3 (and_3_out, or_5_out, or_7_out);
  and and_4 (and_4_out, not_3_out, not_1_out);
  or or_7 (or_7_out, not_3_out, not_2_out, x0);
  or or_8 (or_8_out, and_4_out, and_5_out);
  or or_9 (or_9_out, x3, x2, x1);
  and and_5 (and_5_out, x1, not_1_out);
  and and_6 (and_6_out, or_9_out, or_10_out);
  LED led_1 (.in(and_2_out));
  LED led_2 (.in(and_1_out));
  LED led_3 (.in(and_1_out));
  LED led_4 (.in(and_1_out));
  LED led_5 (.in(or_8_out));
  LED led_6 (.in(or_8_out));
  LED led_7 (.in(or_8_out));
  LED led_8 (.in(and_7_out));
  or or_10 (or_10_out, not_3_out, not_2_out, not_1_out);
  or or_11 (or_11_out, x2, not_2_out, x0);
  LED led_9 (.in(and_2_out));
  LED led_10 (.in(and_2_out));
  LED led_11 (.in(and_3_out));
  LED led_12 (.in(and_3_out));
  LED led_13 (.in(and_3_out));
  LED led_14 (.in(and_6_out));
  LED led_15 (.in(and_6_out));
  LED led_16 (.in(and_6_out));
  LED led_17 (.in(or_11_out));
  LED led_18 (.in(or_11_out));
  LED led_19 (.in(or_11_out));
  LED led_20 (.in(and_7_out));
  LED led_21 (.in(and_7_out));
  or or_12 (or_12_out, x3, x2, x1, not_1_out);
  or or_13 (or_13_out, not_3_out, x1, x0);
  or or_14 (or_14_out, not_3_out, not_2_out, not_1_out);
  and and_7 (and_7_out, or_12_out, or_13_out, or_14_out);
endmodule
