// Logisim project uebung8_2.circ as structural Verilog: 1 circuit, main circuit main
module main (
  input  a,
  input  b,
  input  c,
  input  a_2,
  input  b_2,
  input  c_2,
  output out_7,
  output out_8
);

  wire transistor_1_out, transistor_2_out, transistor_5_out, transistor_10_out, transistor_11_out;

  Transistor #(.\type ("n")) transistor_1 (.in(1'b1), .out(transistor_1_out), .gate(b));
  Transistor #(.\type ("n")) transistor_2 (.in(transistor_1_out), .out(transistor_2_out), .gate(c));
  Transistor transistor_3 (.in(1'b0), .out(transistor_2_out), .gate(c));
  Transistor transistor_4 (.in(1'b0), .out(transistor_2_out), .gate(b));
  Transistor transistor_5 (.in(1'b1), .out(transistor_5_out), .gate(a_2));
  Transistor transistor_6 (.in(transistor_5_out), .out(out_8), .gate(b_2));
  Transistor #(.\type ("n")) transistor_7 (.in(1'b0), .out(out_8), .gate(a_2));
  Transistor transistor_8 (.in(transistor_5_out), .out(out_8), .gate(c_2));
  Transistor #(.\type ("n")) transistor_9 (.in(transistor_10_out), .out(out_8), .gate(c_2));
  Transistor #(.\type ("n")) transistor_10 (.in(1'b0), .out(transistor_10_out), .gate(b_2));
  Transistor transistor_11 (.in(1'b1), .out(transistor_11_out), .gate(a));
  Transistor transistor_12 (.in(transistor_11_out), .out(out_7), .gate(transistor_2_out));
  Transistor #(.\type ("n")) transistor_13 (.in(1'b0), .out(out_7), .gate(a));
  Transistor #(.\type ("n")) transistor_14 (.in(1'b0), .out(out_7), .gate(transistor_2_out));

  // Notes on the sheet:
  //   b AND c
  //   Mischgatter
  //   Standardgatter
endmodule
