// Logisim project volladdierer.circ as structural Verilog: 1 circuit, main circuit main
module main (
  input  cin,
  input  a,
  input  b,
  output sum,
  output cout
);

  wire and_1_out, and_2_out, xor_1_out;

  and and_1 (and_1_out, a, b);
  or or_1 (cout, and_1_out, and_2_out);
  xor xor_1 (xor_1_out, a, b);
  and and_2 (and_2_out, xor_1_out, cin);
  xor xor_2 (sum, cin, xor_1_out);

  // Notes on the sheet:
  //   g
  //   p
endmodule
