// Logisim project zweierkomplementBetragVorzeichenWandler.circ as structural Verilog: 1 circuit, main circuit main
module main (
  input  b3,
  input  b2,
  input  b1,
  input  b0,
  output v,
  output a3,
  output a2,
  output a1,
  output a0
);

  wire and_2_out, and_3_out, and_4_out, and_5_out, and_6_out, and_7_out, and_8_out;

  and and_1 (a3, b3, ~b2, ~b1, ~b0);  // AND_Gate
  and and_2 (and_2_out, b2, ~b1, ~b0);  // AND_Gate
  and and_3 (and_3_out, b3, ~b2, b0);  // AND_Gate
  or or_1 (a2, and_2_out, and_3_out, and_4_out, and_5_out);
  and and_4 (and_4_out, b3, ~b2, b1);  // AND_Gate
  and and_5 (and_5_out, ~b3, b2);  // AND_Gate
  and and_6 (and_6_out, ~b3, b1);  // AND_Gate
  and and_7 (and_7_out, b3, ~b1, b0);  // AND_Gate
  or or_2 (a1, and_7_out, and_6_out, and_8_out);
  and and_8 (and_8_out, b1, ~b0);  // AND_Gate

  assign a0 = b0;
  assign v = b3;
endmodule
